# Fritzing sketch schema (saved by Fritzing 0.8.5b)
breadboards: 1

parts:
  Componente1 = Arduino Leonardo (Rev3b)
  Componente2 = Bluetooth HC-06
  R1 = PHOTOCELL [package=photocell-kit]
  LED1 = LED - 5mm [color="Red (633nm)" package="5 mm [THT]"]
  R2 = Resistor [tolerance=±5% resistance=10k package=THT]
  R3 = Resistor [tolerance=±5% resistance=1 package=THT]

nets:
  N1: Componente1.D2/SDA, R3.Pin_0
  5V: Componente1.5V, Componente2.VCC, R1.P$1
  GND: Componente1.GND, Componente1.D10_PWM/A10, Componente2.TXD, Componente2.GND, LED1.cathode, R2.Pin_1
  N2: Componente1.A0, R1.P$2, R2.Pin_0
  N3: Componente1.D11_PWM, Componente2.RXD
  N4: LED1.anode, R3.Pin_1
